# Fritzing sketch dualrates_example (saved by Fritzing 0.6.3b)

parts:
  Arduino1 = Arduino
  R1 = Rotary Potentiometer (Small) [maximum_resistance=10kΩ]
  S1 = Pushbutton [package=THT]
  R2 = Resistor [tolerance=±5% resistance=10k package=THT]

nets:
  N1: Arduino1.GND, R1.leg2, R2.Pin_0
  N2: Arduino1.D3, S1.leg1, R2.Pin_1
  N3: Arduino1.+5V, R1.leg1, S1.leg0
  N4: Arduino1.A0, R1.wiper
