# Fritzing sketch outputtooutputmix_example (saved by Fritzing 0.6.3b)

parts:
  Arduino1 = Arduino
  R1 = Rotary Potentiometer (Small) [maximum_resistance=10kΩ]

nets:
  N1: Arduino1.GND, R1.leg2
  N2: Arduino1.+5V, R1.leg1
  N3: Arduino1.A0, R1.wiper
