# Fritzing sketch planemodel_example (saved by Fritzing 0.6.3b)

parts:
  Arduino1 = Arduino
  Aileron = Rotary Potentiometer (Small) [maximum_resistance=10kΩ]
  Elevator = Rotary Potentiometer (Small) [maximum_resistance=10kΩ]
  Rudder = Rotary Potentiometer (Small) [maximum_resistance=10kΩ]
  RUD1 = Basic Servo
  ELE1 = Basic Servo
  AIL2 = Basic Servo
  AIL1 = Basic Servo
  FLP1 = Basic Servo
  Flaps = Toggle Switch [package=THT]

nets:
  GND: Arduino1.GND, Aileron.leg2, Elevator.leg2, Rudder.leg2, RUD1.gnd, ELE1.gnd, AIL2.gnd, AIL1.gnd, FLP1.gnd, Flaps.L2
  N1: Arduino1.D7, Flaps.COM
  N2: Arduino1.D6, FLP1.pulse
  N3: Arduino1.D5, RUD1.pulse
  N4: Arduino1.D4, ELE1.pulse
  N5: Arduino1.D3, AIL2.pulse
  N6: Arduino1.D2, AIL1.pulse
  VCC: Arduino1.+5V, Aileron.leg1, Elevator.leg1, Rudder.leg1, RUD1.vcc, ELE1.vcc, AIL2.vcc, AIL1.vcc, FLP1.vcc, Flaps.L1
  N7: Arduino1.A0, Aileron.wiper
  N8: Arduino1.A1, Elevator.wiper
  N9: Arduino1.A2, Rudder.wiper
