# Fritzing sketch retracts_example (saved by Fritzing 0.6.3b)

parts:
  Arduino1 = Arduino
  J3 = Basic Servo
  J4 = Basic Servo
  S1 = Toggle Switch [package=THT]

nets:
  GND: Arduino1.GND, J3.gnd, J4.gnd, S1.L2
  N1: Arduino1.D4, S1.COM
  N2: Arduino1.D3, J3.pulse
  N3: Arduino1.D2, J4.pulse
  VCC: Arduino1.+5V, J3.vcc, J4.vcc, S1.L1
