# Fritzing sketch servoin_example (saved by Fritzing 0.6.3b)

parts:
  Arduino1 = Arduino
  U1 = mystery part, 4 pins [chip_label=RX spacing=300mil]

nets:
  N1: Arduino1.D11, U1.pin1
  N2: Arduino1.D10, U1.pin2
  N3: Arduino1.D9, U1.pin3
  N4: Arduino1.D8, U1.pin4
