# Fritzing sketch swashplate_example (saved by Fritzing 0.6.3b)

parts:
  Arduino1 = Arduino
  R1 = Rotary Potentiometer (Small) [maximum_resistance=10kΩ]
  R3 = Rotary Potentiometer (Small) [maximum_resistance=10kΩ]
  R4 = Rotary Potentiometer (Small) [maximum_resistance=10kΩ]

nets:
  N1: Arduino1.GND, R1.leg2, R3.leg2, R4.leg2
  N2: Arduino1.+5V, R1.leg1, R3.leg1, R4.leg1
  N3: Arduino1.A0, R1.wiper
  N4: Arduino1.A1, R3.wiper
  N5: Arduino1.A2, R4.wiper
