# Fritzing sketch switchtoggler_example (saved by Fritzing 0.6.3b)

parts:
  Arduino1 = Arduino
  S1 = Pushbutton [package=THT]
  R2 = Resistor [tolerance=±5% resistance=10k package=THT]

nets:
  N1: Arduino1.GND, R2.Pin_0
  N2: Arduino1.D3, S1.leg1, R2.Pin_1
  N3: Arduino1.+5V, S1.leg0
