# Fritzing sketch trainer_example (saved by Fritzing 0.6.3b)

parts:
  U1 = mystery part, 1 pin [chip_label=PPM spacing=300mil]
  Arduino2 = Arduino
  AIL = Rotary Potentiometer (Small) [maximum_resistance=10kΩ]
  R4 = Resistor [tolerance=±5% resistance=10k package=THT]
  Trainer = Pushbutton [package=THT]
  ELE = Rotary Potentiometer (Small) [maximum_resistance=10kΩ]
  THR = Rotary Potentiometer (Small) [maximum_resistance=10kΩ]
  RUD = Rotary Potentiometer (Small) [maximum_resistance=10kΩ]

nets:
  N1: U1.pin1, Arduino2.D8
  N2: Arduino2.GND, AIL.leg2, R4.Pin_0, ELE.leg2, THR.leg2, RUD.leg2
  N3: Arduino2.D3, R4.Pin_1, Trainer.leg1
  N4: Arduino2.+5V, AIL.leg1, Trainer.leg0, ELE.leg1, THR.leg1, RUD.leg1
  N5: Arduino2.A0, AIL.wiper
  N6: Arduino2.A1, ELE.wiper
  N7: Arduino2.A2, THR.wiper
  N8: Arduino2.A3, RUD.wiper
