# Fritzing sketch servoout_example (saved by Fritzing 0.6.3b)

parts:
  Arduino1 = Arduino
  R1 = Rotary Potentiometer (Small) [maximum_resistance=10kΩ]
  R3 = Rotary Potentiometer (Small) [maximum_resistance=10kΩ]
  R4 = Rotary Potentiometer (Small) [maximum_resistance=10kΩ]
  R5 = Rotary Potentiometer (Small) [maximum_resistance=10kΩ]
  J1 = Basic Servo
  J2 = Basic Servo
  J3 = Basic Servo
  J4 = Basic Servo

nets:
  GND: Arduino1.GND, R1.leg2, R3.leg2, R4.leg2, R5.leg2, J1.gnd, J2.gnd, J3.gnd, J4.gnd
  N1: Arduino1.D5, J1.pulse
  N2: Arduino1.D4, J2.pulse
  N3: Arduino1.D3, J3.pulse
  N4: Arduino1.D2, J4.pulse
  VCC: Arduino1.+5V, R1.leg1, R3.leg1, R4.leg1, R5.leg1, J1.vcc, J2.vcc, J3.vcc, J4.vcc
  N5: Arduino1.A0, R1.wiper
  N6: Arduino1.A1, R3.wiper
  N7: Arduino1.A2, R4.wiper
  N8: Arduino1.A3, R5.wiper
