# Fritzing sketch switch_example (saved by Fritzing 0.6.3b)

parts:
  Arduino1 = Arduino
  BiState = Pushbutton [package=THT]
  R2 = Resistor [tolerance=±5% resistance=10k package=THT]
  TriState = Toggle Switch [package=THT]
  R3 = Resistor [tolerance=±5% resistance=10k package=THT]
  R4 = Resistor [tolerance=±5% resistance=10k package=THT]

nets:
  N1: Arduino1.GND, R2.Pin_0, R3.Pin_0, R4.Pin_0
  N2: Arduino1.D5, TriState.L2, R3.Pin_1
  N3: Arduino1.D4, TriState.L1, R4.Pin_1
  N4: Arduino1.D3, BiState.leg1, R2.Pin_1
  N5: Arduino1.+5V, BiState.leg0, TriState.COM
