# Fritzing sketch tx_example (saved by Fritzing 0.6.3b)

parts:
  Arduino1 = Arduino
  R1 = Rotary Potentiometer (Small) [maximum_resistance=10kΩ]
  R3 = Rotary Potentiometer (Small) [maximum_resistance=10kΩ]
  R4 = Rotary Potentiometer (Small) [maximum_resistance=10kΩ]
  R5 = Rotary Potentiometer (Small) [maximum_resistance=10kΩ]
  U1 = mystery part, 1 pin [chip_label=? spacing=300mil]
  S1 = Pushbutton [package=THT]
  S2 = Pushbutton [package=THT]
  R6 = Resistor [tolerance=±5% resistance=10k package=THT]
  R7 = Resistor [tolerance=±5% resistance=10k package=THT]

nets:
  N1: Arduino1.GND, R1.leg2, R3.leg2, R4.leg2, R5.leg2, R6.Pin_0, R7.Pin_0
  N2: Arduino1.D9, U1.pin1
  N3: Arduino1.D4, S1.leg0, R6.Pin_1
  N4: Arduino1.D3, S2.leg0, R7.Pin_1
  N5: Arduino1.+5V, R1.leg1, R3.leg1, R4.leg1, R5.leg1, S1.leg1, S2.leg1
  N6: Arduino1.A0, R1.wiper
  N7: Arduino1.A1, R3.wiper
  N8: Arduino1.A2, R4.wiper
  N9: Arduino1.A3, R5.wiper
